// Logisim project board game 4x4.circ as structural Verilog: 3 circuits, main circuit c_4
module c_4 (
  input  [1:0] direction,
  input  CLK,
  output [5:0] earned
);

  wire [1:0] adder_2_out, adder_3_out, multiplexer_1_out, multiplexer_2_out, subtractor_1_out,
       subtractor_2_out, x, y;
  wire [5:0] earned_t, prize;

  // Probe on direction
  Adder #(.width(6)) adder_1 (.a(prize), .b(earned_t), .out(earned));  // open: cin, cout
  Subtractor #(.width(2)) subtractor_1 (.a(x), .b(2'b01), .out(subtractor_1_out));  // open: bin, bout
  Adder #(.width(2)) adder_2 (.a(x), .b(2'b01), .out(adder_2_out));  // open: cin, cout
  // Probe on prize
  board board_1 (.x(x), .y(y), .CLK(CLK), .prize(prize));
  Register #(.width(6)) sum (.D(earned), .Q(earned_t), .clk(CLK));  // open: en, clr
  Multiplexer #(.select(2), .width(2)) multiplexer_1 (
    .in0(x), .in1(x), .in2(subtractor_1_out), .in3(adder_2_out), .out(multiplexer_1_out), .sel(direction));  // open: en
  Register #(.width(2)) u_x (.D(multiplexer_1_out), .Q(x), .clk(CLK));  // open: en, clr
  // Probe on earned
  Subtractor #(.width(2)) subtractor_2 (.a(y), .b(2'b01), .out(subtractor_2_out));  // open: bin, bout
  Adder #(.width(2)) adder_3 (.a(y), .b(2'b01), .out(adder_3_out));  // open: cin, cout
  Multiplexer #(.select(2), .width(2)) multiplexer_2 (
    .in0(subtractor_2_out), .in1(adder_3_out), .in2(y), .in3(y), .out(multiplexer_2_out), .sel(direction));  // open: en
  Register #(.width(2)) u_y (.D(multiplexer_2_out), .Q(y), .clk(CLK));  // open: en, clr

  // Other names for the same wires on the sheet: out[5:0] = earned
endmodule

module board (
  input  [1:0] x,
  input  [1:0] y,
  input  CLK,
  output [5:0] prize
);

  wire multiplexer_1_out, n4_1_equal, n4_2_equal, n4_3_equal, n4_4_equal, n4_5_equal, n4_6_equal, n4_7_equal,
       n4_8_equal, n4_9_equal, n4_10_equal, n4_11_equal, n4_12_equal, n4_13_equal, n4_14_equal, n4_15_equal,
       n4_16_equal, q0, q1, q2, q3, q4, q5, q6, q7, q8, q9, q10, q11, q12, q13, q14, q15;
  wire [1:0] adder_1_out;
  wire [2:2] adder_1_cout;

  _4 u_4_1 (.x({y, x}), .y(4'b0000), .equal(n4_1_equal));
  _4 u_4_2 (.x({y, x}), .y(4'b0100), .equal(n4_2_equal));
  _4 u_4_3 (.x({y, x}), .y(4'b1000), .equal(n4_3_equal));
  _4 u_4_4 (.x({y, x}), .y(4'b1100), .equal(n4_4_equal));
  D_Flip_Flop d_ff_1 (.clk(CLK), .D(1'b1), .Q(q0), .en(n4_1_equal));  // open: Qn, preset, reset
  D_Flip_Flop d_ff_2 (.clk(CLK), .D(1'b1), .Q(q4), .en(n4_2_equal));  // open: Qn, preset, reset
  D_Flip_Flop d_ff_3 (.clk(CLK), .D(1'b1), .Q(q8), .en(n4_3_equal));  // open: Qn, preset, reset
  D_Flip_Flop d_ff_4 (.clk(CLK), .D(1'b1), .Q(q12), .en(n4_4_equal));  // open: Qn, preset, reset
  _4 u_4_5 (.x({y, x}), .y(4'b0001), .equal(n4_5_equal));
  _4 u_4_6 (.x({y, x}), .y(4'b0101), .equal(n4_6_equal));
  _4 u_4_7 (.x({y, x}), .y(4'b1001), .equal(n4_7_equal));
  _4 u_4_8 (.x({y, x}), .y(4'b1101), .equal(n4_8_equal));
  D_Flip_Flop d_ff_5 (.clk(CLK), .D(1'b1), .Q(q1), .en(n4_5_equal));  // open: Qn, preset, reset
  D_Flip_Flop d_ff_6 (.clk(CLK), .D(1'b1), .Q(q5), .en(n4_6_equal));  // open: Qn, preset, reset
  D_Flip_Flop d_ff_7 (.clk(CLK), .D(1'b1), .Q(q9), .en(n4_7_equal));  // open: Qn, preset, reset
  D_Flip_Flop d_ff_8 (.clk(CLK), .D(1'b1), .Q(q13), .en(n4_8_equal));  // open: Qn, preset, reset
  Adder #(.width(2)) adder_1 (.a(x), .b(y), .out(adder_1_out), .cout(adder_1_cout[2]));  // open: cin
  Multiplexer #(.select(4)) multiplexer_1 (
    .in0(q0), .in1(q1), .in2(q2), .in3(q3), .in4(q4), .in5(q5), .in6(q6), .in7(q7), .in8(q8), .in9(q9),
    .in10(q10), .in11(q11), .in12(q12), .in13(q13), .in14(q14), .in15(q15), .out(multiplexer_1_out),
    .sel({y, x}));  // open: en
  _4 u_4_9 (.x({y, x}), .y(4'b0010), .equal(n4_9_equal));
  _4 u_4_10 (.x({y, x}), .y(4'b0110), .equal(n4_10_equal));
  _4 u_4_11 (.x({y, x}), .y(4'b1010), .equal(n4_11_equal));
  _4 u_4_12 (.x({y, x}), .y(4'b1110), .equal(n4_12_equal));
  Multiplexer #(.width(3)) multiplexer_2 (
    .in0({adder_1_cout[2], adder_1_out}), .in1(3'b000), .out(prize[2:0]), .sel(multiplexer_1_out));  // open: en
  D_Flip_Flop d_ff_9 (.clk(CLK), .D(1'b1), .Q(q2), .en(n4_9_equal));  // open: Qn, preset, reset
  D_Flip_Flop d_ff_10 (.clk(CLK), .D(1'b1), .Q(q6), .en(n4_10_equal));  // open: Qn, preset, reset
  D_Flip_Flop d_ff_11 (.clk(CLK), .D(1'b1), .Q(q10), .en(n4_11_equal));  // open: Qn, preset, reset
  D_Flip_Flop d_ff_12 (.clk(CLK), .D(1'b1), .Q(q14), .en(n4_12_equal));  // open: Qn, preset, reset
  _4 u_4_13 (.x({y, x}), .y(4'b0011), .equal(n4_13_equal));
  _4 u_4_14 (.x({y, x}), .y(4'b0111), .equal(n4_14_equal));
  _4 u_4_15 (.x({y, x}), .y(4'b1011), .equal(n4_15_equal));
  _4 u_4_16 (.x({y, x}), .y(4'b1111), .equal(n4_16_equal));
  D_Flip_Flop d_ff_13 (.clk(CLK), .D(1'b1), .Q(q3), .en(n4_13_equal));  // open: Qn, preset, reset
  D_Flip_Flop d_ff_14 (.clk(CLK), .D(1'b1), .Q(q7), .en(n4_14_equal));  // open: Qn, preset, reset
  D_Flip_Flop d_ff_15 (.clk(CLK), .D(1'b1), .Q(q11), .en(n4_15_equal));  // open: Qn, preset, reset
  D_Flip_Flop d_ff_16 (.clk(CLK), .D(1'b1), .Q(q15), .en(n4_16_equal));  // open: Qn, preset, reset

  assign prize[5:3] = 3'b000;

  // Other names for the same wires on the sheet: yx[3:0] = {y, x}
endmodule

module _4 (
  input  [3:0] x,
  input  [3:0] y,
  output equal
);

  wire or_1_out;
  wire [3:0] xor_1_out;

  assign xor_1_out = x ^ y;  // XOR_Gate xor_1, 4 bits wide
  or or_1 (or_1_out, xor_1_out[0], xor_1_out[1], xor_1_out[2], xor_1_out[3]);
  not not_1 (equal, or_1_out);
endmodule
